// Logisim project alu.circ as structural Verilog: 1 circuit, main circuit main
module main (
  input  [1:0] in_1,
  input  in_2,
  input  in_3,
  input  [31:0] in_4,
  input  [31:0] in_5,
  output out_6,
  output [31:0] out_7,
  output out_8
);

  wire and_2_out, and_3_out, and_4_out, and_5_out, or_2_out, or_3_out;
  wire [31:0] adder_1_out, and_1_out, or_1_out, subtractor_1_out;

  Adder #(.width(32)) adder_1 (.a(in_4), .b(in_5), .out(adder_1_out), .cin(in_3));  // open: cout
  Subtractor #(.width(32)) subtractor_1 (.a(in_5), .b(in_4), .out(subtractor_1_out), .bin(in_2));  // open: bout
  assign and_1_out = in_4 & in_5;  // AND_Gate and_1, 32 bits wide
  assign or_1_out = in_4 | in_5;  // OR_Gate or_1, 32 bits wide
  Multiplexer #(.select(2), .width(32), .enable("false")) multiplexer_1 (
    .in0(adder_1_out), .in1(subtractor_1_out), .in2(and_1_out), .in3(or_1_out), .out(out_7), .sel(in_1));
  Multiplexer #(.select(2), .enable("false")) multiplexer_2 (
    .in0(or_2_out), .in1(or_3_out), .in2(1'b0), .in3(1'b0), .out(out_8), .sel(in_1));
  Comparator #(.width(32)) comparator_1 (.a({32{1'b0}}), .b(out_7), .eq(out_6));  // open: gt, lt
  and and_2 (and_2_out, ~adder_1_out[31], in_4[31], in_5[31]);  // AND_Gate
  and and_3 (and_3_out, adder_1_out[31], ~in_4[31], ~in_5[31]);  // AND_Gate
  and and_4 (and_4_out, ~in_4[31], in_5[31], subtractor_1_out[31]);  // AND_Gate
  and and_5 (and_5_out, in_4[31], ~in_5[31], ~subtractor_1_out[31]);  // AND_Gate
  or or_2 (or_2_out, and_2_out, and_3_out);
  or or_3 (or_3_out, and_4_out, and_5_out);
endmodule
