// Logisim project cpu.circ as structural Verilog: 1 circuit, main circuit main
module main (
);

  wire button_1_out, clk_out, main_3_alusrc, main_3_memtoreg, main_3_memwrite, main_3_out_4, main_3_regdst,
       main_7_out_6;
  wire [1:0] main_3_aluctrl, main_3_npcctrl;
  wire [3:0] main_5_r16, main_5_r16_2, main_5_r16_3, main_5_r16_4, main_5_r16_5, main_5_r16_6, main_5_r16_7,
       main_5_r16_8, main_5_r17, main_5_r17_2, main_5_r17_3, main_5_r17_4, main_5_r17_5, main_5_r17_6,
       main_5_r17_7, main_5_r17_8, main_5_r18, main_5_r18_2, main_5_r18_3, main_5_r18_4, main_5_r18_5,
       main_5_r18_6, main_5_r18_7, main_5_r18_8;
  wire [4:0] main_2_out_4, main_2_out_6, main_2_out_8, multiplexer_1_out;
  wire [5:0] main_2_out_2, main_2_out_9;
  wire [15:0] main_2_out_5;
  wire [25:0] main_2_out_7;
  wire [31:0] main_1_out_4, main_2_out_10, main_4_out_2, main_5_qa, main_5_qb, main_5_r8, main_6_out_5,
       main_7_out_7, main_8_out_6, multiplexer_2_out, multiplexer_3_out;

  Clock clk (.out(clk_out));
  Button button_1 (.out(button_1_out));
  pc_main main_1 (.in_1(main_6_out_5), .in_2(clk_out), .in_3(button_1_out), .out_4(main_1_out_4));
  Hex_Digit_Display hex_digit_display_1 (.value(main_5_r8[31:28]));  // open: dp
  im_main main_2 (
    .in_1(main_1_out_4[23:0]), .out_2(main_2_out_2), .out_4(main_2_out_4), .out_5(main_2_out_5),
    .out_6(main_2_out_6), .out_7(main_2_out_7), .out_8(main_2_out_8), .out_9(main_2_out_9),
    .out_10(main_2_out_10));  // open: out_3
  Hex_Digit_Display hex_digit_display_2 (.value(main_5_r8[23:20]));  // open: dp
  Hex_Digit_Display hex_digit_display_3 (.value(main_5_r8[27:24]));  // open: dp
  Hex_Digit_Display hex_digit_display_4 (.value(main_2_out_10[27:24]));  // open: dp
  Hex_Digit_Display hex_digit_display_5 (.value(main_2_out_10[31:28]));  // open: dp
  Hex_Digit_Display hex_digit_display_6 (.value(main_5_r8[19:16]));  // open: dp
  Hex_Digit_Display hex_digit_display_7 (.value(main_5_r8[15:12]));  // open: dp
  cu_main main_3 (
    .in_1(main_2_out_2), .in_2(main_2_out_9), .aluctrl(main_3_aluctrl), .in_3(main_7_out_6),
    .out_4(main_3_out_4), .alusrc(main_3_alusrc), .regdst(main_3_regdst), .memtoreg(main_3_memtoreg),
    .memwrite(main_3_memwrite), .npcctrl(main_3_npcctrl));
  Multiplexer #(.width(5), .enable("false")) multiplexer_1 (
    .in0(main_2_out_4), .in1(main_2_out_6), .out(multiplexer_1_out), .sel(main_3_regdst));
  Hex_Digit_Display hex_digit_display_8 (.value(main_2_out_10[19:16]));  // open: dp
  Hex_Digit_Display hex_digit_display_9 (.value(main_2_out_10[23:20]));  // open: dp
  Hex_Digit_Display hex_digit_display_10 (.value(main_5_r8[7:4]));  // open: dp
  Hex_Digit_Display hex_digit_display_11 (.value(main_5_r8[11:8]));  // open: dp
  ep_main main_4 (.in_1(main_2_out_5), .out_2(main_4_out_2));
  Hex_Digit_Display hex_digit_display_12 (.value(main_2_out_10[11:8]));  // open: dp
  Hex_Digit_Display hex_digit_display_13 (.value(main_2_out_10[15:12]));  // open: dp
  Hex_Digit_Display hex_digit_display_14 (.value(main_5_r8[3:0]));  // open: dp
  Hex_Digit_Display hex_digit_display_15 (.value(main_2_out_10[7:4]));  // open: dp
  Hex_Digit_Display hex_digit_display_16 (.value(main_2_out_10[3:0]));  // open: dp
  rf_main main_5 (
    .clr(button_1_out), .rw(multiplexer_1_out), .clk(clk_out), .we(main_3_out_4),
    .r16({main_5_r16_8, main_5_r16_7, main_5_r16_6, main_5_r16_5, main_5_r16_4, main_5_r16_3, main_5_r16_2, main_5_r16}),
    .r17({main_5_r17_8, main_5_r17_7, main_5_r17_6, main_5_r17_5, main_5_r17_4, main_5_r17_3, main_5_r17_2, main_5_r17}),
    .r18({main_5_r18_8, main_5_r18_7, main_5_r18_6, main_5_r18_5, main_5_r18_4, main_5_r18_3, main_5_r18_2, main_5_r18}),
    .r8(main_5_r8), .qb(main_5_qb), .rb(main_2_out_6), .qa(main_5_qa), .ra(main_2_out_8),
    .data(multiplexer_3_out));
  Multiplexer #(.width(32), .enable("false")) multiplexer_2 (
    .in0(main_5_qb), .in1(main_4_out_2), .out(multiplexer_2_out), .sel(main_3_alusrc));
  npc_main main_6 (
    .in_1(main_3_npcctrl), .in_2(main_1_out_4), .in_3(main_2_out_7), .in_4(main_2_out_5), .out_5(main_6_out_5));
  alu_main main_7 (
    .in_1(main_3_aluctrl), .in_4(main_5_qa), .in_5(multiplexer_2_out), .out_6(main_7_out_6),
    .out_7(main_7_out_7), .in_2(1'b0), .in_3(1'b0));  // open: out_8
  Multiplexer #(.width(32), .enable("false")) multiplexer_3 (
    .in0(main_7_out_7), .in1(main_8_out_6), .out(multiplexer_3_out), .sel(main_3_memtoreg));
  dm_main main_8 (
    .in_1(main_7_out_7[23:0]), .in_2(main_5_qb), .in_3(button_1_out), .in_4(clk_out), .in_5(main_3_memwrite),
    .out_6(main_8_out_6));
  Hex_Digit_Display hex_digit_display_17 (.value(main_5_r18_8));  // open: dp
  Hex_Digit_Display hex_digit_display_18 (.value(main_8_out_6[31:28]));  // open: dp
  Hex_Digit_Display hex_digit_display_19 (.value(main_5_r16_8));  // open: dp
  Hex_Digit_Display hex_digit_display_20 (.value(main_5_r16_7));  // open: dp
  Hex_Digit_Display hex_digit_display_21 (.value(main_5_r17_7));  // open: dp
  Hex_Digit_Display hex_digit_display_22 (.value(main_5_r17_8));  // open: dp
  Hex_Digit_Display hex_digit_display_23 (.value(main_5_r18_6));  // open: dp
  Hex_Digit_Display hex_digit_display_24 (.value(main_5_r18_7));  // open: dp
  Hex_Digit_Display hex_digit_display_25 (.value(main_8_out_6[27:24]));  // open: dp
  Hex_Digit_Display hex_digit_display_26 (.value(main_8_out_6[23:20]));  // open: dp
  Hex_Digit_Display hex_digit_display_27 (.value(main_5_r16_6));  // open: dp
  Hex_Digit_Display hex_digit_display_28 (.value(main_5_r16_5));  // open: dp
  Hex_Digit_Display hex_digit_display_29 (.value(main_5_r17_5));  // open: dp
  Hex_Digit_Display hex_digit_display_30 (.value(main_5_r17_6));  // open: dp
  Hex_Digit_Display hex_digit_display_31 (.value(main_5_r18_4));  // open: dp
  Hex_Digit_Display hex_digit_display_32 (.value(main_5_r18_5));  // open: dp
  Hex_Digit_Display hex_digit_display_33 (.value(main_8_out_6[19:16]));  // open: dp
  Hex_Digit_Display hex_digit_display_34 (.value(main_8_out_6[15:12]));  // open: dp
  Hex_Digit_Display hex_digit_display_35 (.value(main_5_r16_4));  // open: dp
  Hex_Digit_Display hex_digit_display_36 (.value(main_5_r16_3));  // open: dp
  Hex_Digit_Display hex_digit_display_37 (.value(main_5_r17_4));  // open: dp
  Hex_Digit_Display hex_digit_display_38 (.value(main_5_r17_3));  // open: dp
  Hex_Digit_Display hex_digit_display_39 (.value(main_5_r18_2));  // open: dp
  Hex_Digit_Display hex_digit_display_40 (.value(main_5_r18_3));  // open: dp
  Hex_Digit_Display hex_digit_display_41 (.value(main_8_out_6[11:8]));  // open: dp
  Hex_Digit_Display hex_digit_display_42 (.value(main_8_out_6[7:4]));  // open: dp
  Hex_Digit_Display hex_digit_display_43 (.value(main_5_r16));  // open: dp
  Hex_Digit_Display hex_digit_display_44 (.value(main_5_r16_2));  // open: dp
  Hex_Digit_Display hex_digit_display_45 (.value(main_5_r17));  // open: dp
  Hex_Digit_Display hex_digit_display_46 (.value(main_5_r17_2));  // open: dp
  Hex_Digit_Display hex_digit_display_47 (.value(main_5_r18));  // open: dp
  Hex_Digit_Display hex_digit_display_48 (.value(main_8_out_6[3:0]));  // open: dp

  // Notes on the sheet:
  //   reset
endmodule
