// Logisim project cu.circ as structural Verilog: 1 circuit, main circuit main
module main (
  input  [5:0] in_1,
  input  [5:0] in_2,
  input  in_3,
  output out_4,
  output alusrc,
  output regdst,
  output memtoreg,
  output memwrite,
  output [1:0] npcctrl,
  output [1:0] aluctrl
);

  wire and_1_out, and_2_out, and_3_out, and_4_out, and_5_out, and_7_out, and_8_out, and_9_out, and_10_out,
       and_11_out, and_12_out, or_6_out;
  wire [1:0] multiplexer_1_out;

  and and_1 (and_1_out, in_1[5], ~in_1[4], ~in_1[3], ~in_1[2], ~in_1[1], ~in_1[0]);  // AND_Gate
  and and_2 (and_2_out, and_1_out, and_5_out);
  and and_3 (and_3_out, in_1[5], ~in_1[4], ~in_1[3], ~in_1[2], in_1[1], ~in_1[0]);  // AND_Gate
  and and_4 (and_4_out, and_5_out, and_3_out);
  and and_5 (and_5_out, ~in_2[5], ~in_2[4], ~in_2[3], ~in_2[2], ~in_2[1], ~in_2[0]);  // AND_Gate
  and and_6 (aluctrl[1], ~in_2[5], ~in_2[4], in_2[3], in_2[2], ~in_2[1], in_2[0]);  // AND_Gate
  and and_7 (and_7_out, in_2[5], ~in_2[4], ~in_2[3], ~in_2[2], in_2[1], in_2[0]);  // AND_Gate
  and and_8 (and_8_out, in_2[5], ~in_2[4], in_2[3], ~in_2[2], in_2[1], in_2[0]);  // AND_Gate
  and and_9 (and_9_out, ~in_2[5], ~in_2[4], ~in_2[3], in_2[2], ~in_2[1], ~in_2[0]);  // AND_Gate
  and and_10 (and_10_out, ~in_2[5], ~in_2[4], ~in_2[3], ~in_2[2], in_2[1], ~in_2[0]);  // AND_Gate
  and and_11 (and_11_out, ~in_2[5], ~in_2[4], in_2[3], ~in_2[2], ~in_2[1], ~in_2[0]);  // AND_Gate
  or or_1 (out_4, and_5_out, and_11_out, aluctrl[1], and_7_out, and_7_out);
  or or_2 (alusrc, aluctrl[1], aluctrl[1], and_11_out, and_7_out, and_8_out, and_8_out, and_8_out);
  or or_3 (regdst, and_11_out, and_5_out, and_7_out);
  or or_4 (memtoreg, and_7_out, and_7_out, and_7_out);
  or or_5 (memwrite, and_8_out, and_8_out, and_8_out);
  and and_12 (and_12_out, and_9_out, in_3, in_3);
  or or_6 (or_6_out, and_7_out, and_8_out, and_8_out);
  or or_7 (aluctrl[0], and_4_out, and_9_out, and_9_out);
  Multiplexer #(.width(2), .enable("false")) multiplexer_1 (
    .in0(2'b00), .in1(2'b01), .out(multiplexer_1_out), .sel(and_12_out));
  Multiplexer #(.width(2), .enable("false")) multiplexer_2 (
    .in0(multiplexer_1_out), .in1(2'b10), .out(npcctrl), .sel(and_10_out));

  // Notes on the sheet:
  //   add
  //   sub
  //   addi
  //   regwrite
  //   extop
endmodule
