// Logisim project ep.circ as structural Verilog: 1 circuit, main circuit main
module main (
  input  [15:0] in_1,
  output [31:0] out_2
);

  assign out_2 = {{16{in_1[15]}}, in_1};  // Bit_Extender bit_extender_1
endmodule
