// Logisim project im.circ as structural Verilog: 1 circuit, main circuit main
module main (
  input  [23:0] in_1,
  output [5:0] out_2,
  output [4:0] out_3,
  output [4:0] out_4,
  output [15:0] out_5,
  output [4:0] out_6,
  output [25:0] out_7,
  output [4:0] out_8,
  output [5:0] out_9,
  output [31:0] out_10
);

  ROM #(.addrWidth(24), .dataWidth(32)) rom_1 (
    .addr(in_1), .data({out_9, out_7[25:21], out_6, out_4, out_3, out_2}));  // open: sel

  assign out_5 = {out_4, out_3, out_2};
  assign out_7[20:0] = {out_6, out_4, out_3, out_2};
  assign out_8 = out_7[25:21];
  assign out_10 = {out_9, out_7[25:21], out_6, out_4, out_3, out_2};
endmodule
