// Logisim project npc.circ as structural Verilog: 1 circuit, main circuit main
module main (
  input  [1:0] in_1,
  input  [31:0] in_2,
  input  [25:0] in_3,
  input  [15:0] in_4,
  output [31:0] out_5
);

  wire [31:0] adder_1_out, adder_2_out, bit_extender_1_out;

  assign bit_extender_1_out = {{16{in_4[15]}}, in_4};  // Bit_Extender bit_extender_1
  Adder #(.width(32)) adder_1 (.a(in_2), .b(32'h4), .out(adder_1_out));  // open: cin, cout
  Multiplexer #(.select(2), .width(32), .enable("false")) multiplexer_1 (
    .in0(adder_1_out), .in1(adder_2_out), .in2({in_2[31:28], in_3, 2'b00}), .out(out_5), .sel(in_1));  // open: in3
  Adder #(.width(32)) adder_2 (
    .a(adder_1_out), .b({bit_extender_1_out[29:0], 2'b00}), .out(adder_2_out));  // open: cin, cout
endmodule
