// Logisim project pc.circ as structural Verilog: 1 circuit, main circuit main
module main (
  input  [31:0] in_1,
  input  in_2,
  input  in_3,
  output [31:0] out_4
);

  Register #(.width(32)) register_1 (.D(in_1), .Q(out_4), .clk(in_2), .clr(in_3));  // open: en
endmodule
